# Fritzing sketch Game Board with Arduino Mega (saved by Fritzing 0.9.3b)
breadboards: 1

parts:
  R6 = Resistor [tolerance=±5% resistance=4.7k package=THT]
  R9 = Resistor [tolerance=±5% resistance=4.7k package=THT]
  S1 = Pushbutton [package="[THT]"]
  S2 = Pushbutton [package="[THT]"]
  Part2 = Adafruit RGB LCD Pi Plate [part_number="Adafruit #1109 #1110 "]
  S3 = Pushbutton [package="[THT]"]
  R3 = Resistor [tolerance=±5% resistance=220 package=THT]
  Part6 = Arduino Mega 2560 (Rev3)
  U1 = 6N139 Optoisolator [part_number=6N139 chip_label=6N139 package="DIP (Dual Inline) [THT]"]
  R2 = Resistor [tolerance=±5% resistance=10k package=THT]
  R1 = Resistor [tolerance=±5% resistance=10k package=THT]
  LED2 = LED - 3mm [color="Green (555nm)" package="3 mm [THT]"]
  LED3 = LED - 3mm [color="Blue (430nm)" package="3 mm [THT]"]
  LED1 = LED - 3mm [color="Red (633nm)" package="3 mm [THT]"]
  U2 = 6N139 Optoisolator [part_number=6N139 chip_label=6N139 package="DIP (Dual Inline) [THT]"]
  R8 = Resistor [tolerance=±5% resistance=10k package=THT]
  U3 = 6N139 Optoisolator [part_number=6N139 chip_label=6N139 package="DIP (Dual Inline) [THT]"]
  R5 = Resistor [tolerance=±5% resistance=10k package=THT]
  R4 = Resistor [tolerance=±5% resistance=220 package=THT]
  R11 = Resistor [tolerance=±5% resistance=220 package=THT]
  IC2 = 74HCT08 [package="DIP (Dual Inline) [THT]"]

nets:
  5V: R6.Pin_0, R9.Pin_0, Part2.+5V, R3.Pin_0, Part6.5V, U1.Vcc, R2.Pin_1, R1.Pin_1, U2.Vcc, R8.Pin_1, U3.Vcc, R5.Pin_1, IC2.Vcc
  N1: R6.Pin_1, LED1.anode
  N2: R9.Pin_1, LED2.anode
  AND2B/Pin_D41: S1.Pin_1, S1.Pin_2, Part6.D41, IC2.2B
  Pin_D39: S1.Pin_3, S1.Pin_4, Part6.D39
  AND1B/Pin_D47: S2.Pin_1, S2.Pin_2, Part6.D47, IC2.1B
  Pin_D45: S2.Pin_3, S2.Pin_4, Part6.D45
  N3: Part2.SDA, Part6.D20/SDA, Part6.SDA
  N4: Part2.SCL, Part6.SCL
  GND: Part2.GND, Part6.GND, U1.GND, U2.GND, U3.GND, IC2.GND
  AND1A/Pin_D53: S3.Pin_1, S3.Pin_2, Part6.D53, IC2.1A
  Pin_D51: S3.Pin_3, S3.Pin_4, Part6.D51
  N5: R3.Pin_1, LED3.anode
  3.3V: Part6.3V3
  INT_1: Part6.D2_PWM, R1.Pin_0, R4.Pin_1, R11.Pin_1
  Pin_D37: Part6.D37, U3.cathode
  Pin_D43: Part6.D43, U2.cathode
  Pin_D49: Part6.D49, U1.cathode
  N6: U1.anode, R2.Pin_0
  N7: U1.Vo, LED3.cathode
  N8: LED2.cathode, U2.Vo
  N9: LED1.cathode, U3.Vo
  N10: U2.anode, R8.Pin_0
  N11: U3.anode, R5.Pin_0
  N12: R4.Pin_0, IC2.1Y, IC2.2A
  N13: R11.Pin_0, IC2.2Y

notes:
  TARGET LIGHTS AND BUTTONS
  Game Board, 3b
  +5V to Pin 2 for LED enable,
  D49=LOW for LED on
  D51=LOW for Switch enable,
  Switch closed to ground pins INT_1 (shared) and D53 (single)

custom parts:
  Adafruit RGB LCD Pi Plate: This new Adafruit Pi Plate makes it easy to use an RGB 16x2 Character LCD. We really like the RGB Character LCDs we stock in the shop. (For RGB we have RGB negative and RGB positive.) Unfortunately, these LCDs do require quite a few digital pins, 6 to control the LCD and then another 3 to control the RGB backlight for a total of 9 pins. That's nearly all the GPIO available on a Pi! With this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
  6N139 Optoisolator: 6N139 Optoisolator. 8-DIP, 300mil
  74HCT08: Quad 2 input AND gates
