# Fritzing sketch Target 4x Rev 1 (saved by Fritzing 0.9.3b)
circuit board: 8cm x 8cm
breadboards: 1

parts:
  R2 = Resistor [tolerance=±5% resistance=220 package=THT]
  R4 = Resistor [tolerance=±5% resistance=220 package=THT]
  S1 = Pushbutton [package="[THT]"]
  S2 = Pushbutton [package="[THT]"]
  S4 = Pushbutton [package="[THT]"]
  R8 = Resistor [tolerance=±5% resistance=220 package=THT]
  U4 = 6N139 Optoisolator [part_number=6N139 chip_label=6N139 package="DIP (Dual Inline) [THT]"]
  R7 = Resistor [tolerance=±5% resistance=10k package=THT]
  R11 = Resistor [tolerance=±5% resistance=10k package=THT]
  LED2 = LED - 3mm [color="Green (555nm)" package="3 mm [THT]"]
  LED4 = LED - 3mm [color="Blue (430nm)" package="3 mm [THT]"]
  LED1 = LED - 3mm [color="Red (633nm)" package="3 mm [THT]"]
  U2 = 6N139 Optoisolator [part_number=6N139 chip_label=6N139 package="DIP (Dual Inline) [THT]"]
  R3 = Resistor [tolerance=±5% resistance=10k package=THT]
  U1 = 6N139 Optoisolator [part_number=6N139 chip_label=6N139 package="DIP (Dual Inline) [THT]"]
  R1 = Resistor [tolerance=±5% resistance=10k package=THT]
  R9 = Resistor [tolerance=±5% resistance=220 package=THT]
  R10 = Resistor [tolerance=±5% resistance=220 package=THT]
  U5 = 74HCT08 [package="DIP (Dual Inline) [THT]"]
  J11 = female pin header, 1 pin [form="♀ (female)"]
  J1 = female pin header, 2 pins [form="♀ (female)"]
  U3 = 6N139 Optoisolator [part_number=6N139 chip_label=6N139 package="DIP (Dual Inline) [THT]"]
  R6 = Resistor [tolerance=±5% resistance=220 package=THT]
  S3 = Pushbutton [package="[THT]"]
  LED3 = LED - 3mm [color="Yellow (595nm)" package="3 mm [THT]"]
  J2 = female pin header, 2 pins [form="♀ (female)"]
  R5 = Resistor [tolerance=±5% resistance=10k package=THT]
  J10 = female pin header, 2 pins [form="♀ (female)"]
  J9 = female pin header, 2 pins [form="♀ (female)"]
  J8 = female pin header, 2 pins [form="♀ (female)"]
  J7 = female pin header, 2 pins [form="♀ (female)"]
  J6 = screw terminal, 3 pins
  J4 = screw terminal, 3 pins
  J3 = screw terminal, 3 pins
  J5 = screw terminal, 3 pins

nets:
  12V: R2.Pin_0, R4.Pin_0, R8.Pin_0, U4.Vcc, U2.Vcc, U1.Vcc, J1.pin1, U3.Vcc, R6.Pin_0
  N1: R2.Pin_1, LED1.anode
  N2: R4.Pin_1, LED2.anode
  AND1A/Pin_D41: S1.Pin_1, S1.Pin_2, U5.1A, J7.pin2, J3.pin3
  Pin_D39: S1.Pin_3, S1.Pin_4, J7.pin1, J3.pin2
  AND1B/Pin_D47: S2.Pin_1, S2.Pin_2, U5.1B, J8.pin2, J4.pin3
  Pin_D45: S2.Pin_3, S2.Pin_4, J8.pin1, J4.pin2
  AND2B/Pin_D53: S4.Pin_1, S4.Pin_2, U5.2B, J10.pin2, J6.pin3
  Pin_D51: S4.Pin_3, S4.Pin_4, J10.pin1, J6.pin2
  N3: R8.Pin_1, LED4.anode
  N4: U4.anode, R7.Pin_0
  Pin_D49: U4.cathode, J6.pin1
  GND: U4.GND, U2.GND, U1.GND, J1.pin2, U3.GND
  N5: U4.Vo, LED4.cathode
  5V: R7.Pin_1, R11.Pin_1, R3.Pin_1, R1.Pin_1, U5.Vcc, J2.pin1, R5.Pin_1
  INT_1: R11.Pin_0, R9.Pin_1, R10.Pin_1, J11.pin1
  N6: LED2.cathode, U2.Vo
  N7: LED1.cathode, U1.Vo
  N8: U2.anode, R3.Pin_0
  Pin_D43: U2.cathode, J4.pin1
  N9: U1.anode, R1.Pin_0
  Pin_D37: U1.cathode, J3.pin1
  N10: R9.Pin_0, U5.1Y
  N11: R10.Pin_0, U5.2Y
  AND2A/Pin_D35: U5.2A, S3.Pin_1, S3.Pin_2, J9.pin2, J5.pin3
  N12: U5.GND, J2.pin2
  N13: U3.anode, R5.Pin_0
  Pin_D31: U3.cathode, J5.pin1
  N14: U3.Vo, LED3.cathode
  N15: R6.Pin_1, LED3.anode
  Pin_D33: S3.Pin_3, S3.Pin_4, J9.pin1, J5.pin2

notes:
  Game Board, 1
  L I O
  INT
  +5V
  +LED
  C.Dudzek
  2-Apr-2018

custom parts:
  6N139 Optoisolator: 6N139 Optoisolator. 8-DIP, 300mil
  74HCT08: Quad 2 input AND gates
